# Fritzing sketch PSoC prototyping Kit DCO (saved by Fritzing 0.9.2b)
breadboards: 1

parts:
  U1 = mystery part, 44 pins [chip_label=" PSoC 4 Prototyping Kit"]
  R1 = Resistor [tolerance=±5% resistance=1k package=THT]
  J1 = STM32 Nucleo boards
  R2 = Resistor [tolerance=±5% resistance=1k package=THT]
  C1 = Ceramic Capacitor [capacitance=100nF package="100 mil [THT, multilayer]"]

nets:
  N1: U1.pin10, J1.D11_PWM/MOSI
  N2: U1.pin11, J1.D13/SCK
  N3: U1.pin12, J1.D9_PWM
  N4: U1.pin13, U1.pin14, R1.Pin_0
  N5: U1.pin15, R2.Pin_1
  N6: U1.pin21, R1.Pin_1, J1.GND, C1.0
  N7: R2.Pin_0, C1.1

notes:
  Wave Out
  GND
  +3.3V
