# Fritzing sketch PSoC4 Prototyping Kit DCO Test (saved by Fritzing 0.9.2b)
breadboards: 1

parts:
  R1 = Resistor [tolerance=±5% resistance=1k package=THT]
  U1 = mystery part, 44 pins [chip_label="PSoC 4 Prototyping Kit"]

nets:
  N1: R1.Pin_0, U1.pin13, U1.pin14
  N2: R1.Pin_1, U1.pin21

notes:
  Wave Out
  GND
  +3.3V
