# Fritzing sketch PSoC4 DCO (saved by Fritzing 0.9.2b)
perfboards: 2
breadboards: 3

parts:
  LCD1 = LCD screen
  R1 = Resistor [tolerance=±5% resistance=1k package=THT]
  R2 = TRIMPOT [package=3362u-2]
  J1 = female pin header, 8 pins [form="♀ (female)"]
  J2 = female pin header, 9 pins [form="♀ (female)"]
  J3 = female pin header, 10 pins [form="♀ (female)"]
  J4 = female pin header, 8 pins [form="♀ (female)"]
  J5 = female pin header, 9 pins [form="♀ (female)"]
  R3 = Resistor [tolerance=±5% resistance=1k package=THT]
  S1 = Pushbutton [package="[THT]"]
  S2 = Pushbutton [package="[THT]"]
  S3 = Pushbutton [package="[THT]"]
  S4 = Pushbutton [package="[THT]"]
  S5 = Pushbutton [package="[THT]"]
  S6 = Pushbutton [package="[THT]"]
  S7 = Pushbutton [package="[THT]"]
  S8 = Pushbutton [package="[THT]"]
  J6 = female pin header, 6 pins [form="♀ (female)"]
  J7 = female pin header, 6 pins [form="♀ (female)"]
  パーツ1 = Arduino Uno (Rev3)
  IC1 = IC, DIP package, 16 pins [chip_label=74HC4050]
  U1 = mystery part, 8 pins [chip_label=Nokia5110]
  R4 = Rotary Potentiometer (Small) [maximum_resistance=100kΩ package=THT]
  RE1 = Rotary Encoder [package=THT]

nets:
  N1: LCD1.VSS, LCD1.LED-, R2.CW, J1.pin6, R3.Pin_0
  N2: LCD1.VDD, R1.Pin_0, R2.CCW, J1.pin5
  N3: LCD1.V0, R2.WIPER
  N4: LCD1.RS, J2.pin6
  N5: LCD1.R/W, J3.pin10
  N6: LCD1.E, J2.pin5
  N7: LCD1.DB4, J2.pin1
  N8: LCD1.DB5, J2.pin2
  N9: LCD1.DB6, J2.pin3
  N10: LCD1.DB7, J2.pin4
  N11: LCD1.LED+, R1.Pin_1
  N12: J2.pin7, RE1.EncoderPinA
  N13: J2.pin8, RE1.EncoderPinB
  N14: J2.pin9, J5.pin9, R3.Pin_1
  N15: J3.pin1, J7.pin5
  N16: J3.pin2, J6.pin5
  N17: J3.pin4, パーツ1.GND, IC1.pin8, U1.pin2, U1.pin8, R4.leg1, RE1.EncoderPinC
  N18: J3.pin5, パーツ1.D13/SCK, IC1.pin9
  N19: J4.pin6, パーツ1.D9_PWM
  N20: J4.pin7, パーツ1.D12/MISO
  N21: J4.pin8, パーツ1.D11_PWM/MOSI, IC1.pin11
  N22: S1.Pin_1, S1.Pin_2
  N23: S1.Pin_3, S1.Pin_4
  N24: S2.Pin_1, S2.Pin_2
  N25: S2.Pin_3, S2.Pin_4
  N26: S3.Pin_1, S3.Pin_2
  N27: S3.Pin_3, S3.Pin_4
  N28: S4.Pin_1, S4.Pin_2
  N29: S4.Pin_3, S4.Pin_4
  N30: S5.Pin_1, S5.Pin_2
  N31: S5.Pin_3, S5.Pin_4
  N32: S6.Pin_1, S6.Pin_2
  N33: S6.Pin_3, S6.Pin_4
  N34: S7.Pin_1, S7.Pin_2
  N35: S7.Pin_3, S7.Pin_4
  N36: S8.Pin_1, S8.Pin_2
  N37: S8.Pin_3, S8.Pin_4
  N38: パーツ1.A0, R4.wiper
  N39: パーツ1.D10_PWM/SS, IC1.pin3
  N40: パーツ1.D2, IC1.pin7
  N41: パーツ1.D3_PWM, IC1.pin5
  N42: パーツ1.3V3, IC1.pin1, U1.pin1
  N43: パーツ1.5V, R4.leg2
  N44: IC1.pin2, U1.pin3
  N45: IC1.pin4, U1.pin4
  N46: IC1.pin6, U1.pin5
  N47: IC1.pin10, U1.pin7
  N48: IC1.pin12, U1.pin6

notes:
  PSoC 4 Pioneer Kit
  Tact Switchs
  WaveOut
  Check1/Check2
